// Logisim project Questão 1-B.circ as structural Verilog: 1 circuit, main circuit main
module main (
  input  a,
  input  b,
  output x
);

  wire not_1_out, not_2_out;

  not not_1 (not_1_out, a);
  not not_2 (not_2_out, b);
  nand nand_1 (x, not_1_out, not_2_out);
endmodule
